// Digital circuit 8bitALUNew.dig as structural Verilog
module _8bitALUNew (
  input  [7:0] A,
  input  [7:0] B,
  input  [2:0] Carry,
  output status,
  output [7:0] \output 
);

  wire [7:0] multiplexer_1_out, not_1_out, not_2_out;

  assign not_1_out = ~B;  // Not not_1, 8 bits wide
  assign not_2_out = ~{8{1'b0}};  // Not not_2, 8 bits wide
  Multiplexer #(.Selector_Bits(2), .Bits(8)) multiplexer_1 (
    .sel(Carry[2:1]), .in_0(B), .in_1(not_1_out), .in_2({8{1'b0}}), .in_3(not_2_out), .out(multiplexer_1_out));
  // _8bitadder _8bitadder_1: pin names not known; wires that end beside it: A, multiplexer_1_out, Carry[0], status, \output 
endmodule
