// Digital circuit RegisterFile.dig as structural Verilog
module RegisterFile (
  input  [1:0] Read_register1,
  input  [1:0] Read_register2,
  input  CLK,
  input  [7:0] Write_register,
  input  [7:0] Write_data,
  input  [1:0] CTRL,
  output [7:0] Data1,
  output [7:0] Data2
);

  wire [7:0] demultiplexer_1_out_0, demultiplexer_1_out_1, demultiplexer_1_out_2, demultiplexer_1_out_3,
       R_0_p4, R_1_p4, R_2_p4, R_3_p4;

  Demultiplexer #(.Bits(8), .Selector_Bits(2)) demultiplexer_1 (
    .sel(CTRL), .in(Write_register), .out_0(demultiplexer_1_out_0), .out_1(demultiplexer_1_out_1),
    .out_2(demultiplexer_1_out_2), .out_3(demultiplexer_1_out_3));
  // GPR R_0: pin names not known; wires that end beside it: demultiplexer_1_out_0, Write_data[1:0], CLK, R_0_p4
  // GPR R_1: pin names not known; wires that end beside it: demultiplexer_1_out_1, Write_data[3:2], CLK, R_1_p4
  // GPR R_2: pin names not known; wires that end beside it: demultiplexer_1_out_2, Write_data[5:4], CLK, R_2_p4
  // GPR R_3: pin names not known; wires that end beside it: demultiplexer_1_out_3, Write_data[7:6], CLK, R_3_p4
  Multiplexer #(.Bits(8), .Selector_Bits(2)) multiplexer_1 (
    .sel(Read_register1), .in_0(R_0_p4), .in_1(R_1_p4), .in_2(R_2_p4), .in_3(R_3_p4), .out(Data1));
  Multiplexer #(.Selector_Bits(2), .Bits(8)) multiplexer_2 (
    .sel(Read_register2), .in_0(R_0_p4), .in_1(R_1_p4), .in_2(R_2_p4), .in_3(R_3_p4), .out(Data2));
endmodule
